# Fritzing sketch var01 (saved by Fritzing 0.9.3b)
breadboards: 1

parts:
  XTAL1 = Crystal [frequency="16 Mhz" package=SMD]
  C1 = Capacitor [part_number=22pf package=0603-cap]
  C2 = Capacitor [part_number=22pf package=0603-cap]
  LED1 = Super Flux RGB LED (com. anode)  # not connected
  U1 = ATMEGA168 [package=tqfp]  # not connected
  S1 = Pushbutton [package="[SMD]"]  # not connected
  Y1 = Resonator [frequency="16 Mhz" package=THT]  # not connected
  Y2 = Resonator [package=resonator-smd]  # not connected

nets:
  N1: XTAL1.pin_0, C2.1
  N2: XTAL1.pin_1, C1.1
  GND: C1.2, C2.2
